# Fritzing sketch Coche (saved by Fritzing 0.9.9b)

parts:
  Componente1 = NRF24L01+ Breakout Board  # not connected
  Componente2 = Arduino Nano (Rev3.0) (ICSP)
  Componente3 = Motor Driver 1A Dual TB6612FNG
  U1 = RELAY [package=relay-g5q]
  M2 = DC Motor  # not connected
  M3 = DC Motor  # not connected
  LED1 = LED - 5mm [color="Red (633nm)" current=0.030 package="5 mm [THT]"]  # not connected
  BAT1 = Battery Holders [package=battery-aa]
  BAT2 = Battery Holders [package=battery-aa]
  BAT3 = Battery Holders [package=battery-aa]
  R1 = Resistor [tolerance=±5% resistance=220 package="2010 [SMD]"]
  U2 = TRANSISTOR_NPN_2 [package=to-92]
  D1 = P1000K [part_number=P1000K]

nets:
  GND: Componente2.GND, Componente3.GND, BAT2.-, U2.E
  N1: Componente2.VIN, BAT1.-, BAT3.+
  N2: U1.COIL2, U2.C, D1.anode
  N3: U1.COIL1, D1.cathode
  N4: BAT2.+, BAT3.-
  N5: R1.Pin_1, U2.B
