# Fritzing sketch Control (saved by Fritzing 0.9.9b)

parts:
  Componente1 = Arduino Nano (Rev3.0)
  Componente2 = NRF24L01+ Breakout Board
  Componente3 = Thumb Joystick
  Componente4 = Thumb Joystick
  C1 = Capacitor Polarized [package=cpol-radial-10uf-25v]
  LED1 = LED - 5mm [color="Red (633nm)" current=0.030 package="5 mm [THT]"]
  U3 = SWITCH-SPST-2 [package=r_sw_th]
  S1 = Round Pushbutton
  S2 = Round Pushbutton
  S3 = Round Pushbutton
  S4 = Round Pushbutton
  IC1 = Voltage Regulator LM1117 [package=sot223]
  VCC1 = Battery block 9V
  U4 = POT [package=pot_mammoth]
  S5 = Square Pushbutton

nets:
  GND: Componente1.GND, Componente2.GND, Componente3.GND, Componente4.GND, C1.-, LED1.cathode, S1.leg1, S2.leg1, S3.leg1, S4.leg1, IC1.ADJ, VCC1.-, U4.E, S5.leg1
  N1: Componente1.D2, S2.leg0
  N2: Componente1.D3, S1.leg0
  N3: Componente1.D4, S3.leg0
  N4: Componente1.D5, S4.leg0
  N5: Componente1.D6, S5.leg0
  N6: Componente1.D7, Componente3.SEL
  N7: Componente1.D8, Componente4.SEL
  N8: Componente1.D9, Componente2.CE
  N9: Componente1.D10, Componente2.CS
  N10: Componente1.D11/MOSI, Componente2.MOSI
  N11: Componente1.D12/MISO, Componente2.MISO
  N12: Componente1.VIN, U3.O, IC1.IN
  VCC: Componente1.5V, Componente3.VCC, Componente4.VCC, U4.A
  N13: Componente1.A4, LED1.anode, U4.S
  N14: Componente1.A3, Componente3.VERT
  N15: Componente1.A2, Componente3.HORZ
  N16: Componente1.A1, Componente4.VERT
  N17: Componente1.A0, Componente4.HORZ
  N18: Componente1.D13/SCK, Componente2.SCK
  N19: Componente2.VCC, C1.+, IC1.OUT
  N20: U3.P, VCC1.+
